# Fritzing sketch diagram (saved by Fritzing 0.9.9b)
breadboards: 2

parts:
  Part1 = Arduino Uno (Rev3) - ICSP
  LED1 = LED - 5mm [color="Red (633nm)" current=0.030 package="5 mm [THT]"]
  R3 = PHOTOCELL [package=photocell]
  S2 = Pushbutton [package="[THT]"]
  S1 = Pushbutton [package="[THT]"]
  R4 = Resistor [tolerance=±5% resistance=10k package="2512 [SMD]"]
  LED3 = LED - 5mm [color="Yellow (595nm)" current=0.030 package="5 mm [THT]"]
  R5 = Resistor [tolerance=±5% resistance=220 package="2512 [SMD]"]
  R6 = Resistor [tolerance=±5% resistance=220 package="2512 [SMD]"]
  R7 = Resistor [tolerance=±5% resistance=220 package="2512 [SMD]"]
  LED4 = LED - 5mm [color="Green (555nm)" current=0.030 package="5 mm [THT]"]

nets:
  N1: Part1.A0, R3.P$1, R4.Pin_1
  N2: Part1.A2, R7.Pin_0, LED4.anode
  N3: Part1.A3, LED1.anode, R6.Pin_0
  N4: Part1.ICSP_MISO, Part1.D12/MISO, S1.Pin_1, S1.Pin_2
  N5: Part1.ICSP_MOSI, Part1.D11_PWM/MOSI, S2.Pin_1, S2.Pin_2
  N6: Part1.GND, Part1.D2, LED1.cathode, S2.Pin_3, S2.Pin_4, S1.Pin_3, S1.Pin_4, R4.Pin_0, R5.Pin_0, LED4.cathode
  N7: Part1.D8, LED3.anode
  N8: Part1.D9_PWM, R6.Pin_1
  N9: Part1.D10_PWM/SS, R7.Pin_1
  N10: Part1.5V, R3.P$2
  N11: LED3.cathode, R5.Pin_1
